// Logisim project cpu.circ as structural Verilog: 2 circuits, main circuit main
module main (
  input  LOAD_TOKEN_IN,
  input  FTIN,
  input  STORE_TOKEN_IN,
  input  [31:0] LOAD_DATA,
  input  TIN,
  input  CLK,
  input  [31:0] RAMIRIN,
  input  TRAMIRIN,
  output [3:0] LOAD_BYTE_W,
  output [3:0] STORE_BYTE_W,
  output LOAD_TOKEN_OUT,
  output [23:0] LOAD_ADDR,
  output STORE_TOKEN_OUT,
  output [23:0] STORE_ADDR,
  output [31:0] STORE_DATA,
  output [23:0] RAMIRADDR,
  output TRAMIROUT,
  output TOUT
);

  wire ALU_ACT, ALU_SINK, and_3_out, and_7_out, and_8_out, and_11_out, C0x0T, C0x1T, C0x2T, C0x3T,
       comparator_1_gt, comparator_1_lt, comparator_4_eq, comparator_5_eq, d_ff_1_q, d_ff_4_q, d_ff_5_q,
       d_ff_13_q, d_ff_14_q, d_ff_15_q, d_ff_17_q, d_ff_23_q, d_ff_24_q, demultiplexer_2_out1,
       demultiplexer_2_out2, demultiplexer_2_out3, demultiplexer_2_out4, demultiplexer_2_out5,
       demultiplexer_2_out6, demultiplexer_6_out7, demultiplexer_6_out9, demultiplexer_6_out10,
       demultiplexer_6_out11, demultiplexer_6_out12, demultiplexer_6_out14, demultiplexer_6_out15,
       demultiplexer_7_out8, demultiplexer_7_out9, demultiplexer_8_out0, demultiplexer_8_out1,
       demultiplexer_8_out2, demultiplexer_8_out3, demultiplexer_9_out0, demultiplexer_9_out1,
       demultiplexer_9_out2, demultiplexer_9_out3, demultiplexer_9_out4, demultiplexer_9_out5,
       demultiplexer_9_out10, demultiplexer_9_out11, demultiplexer_9_out12, demultiplexer_9_out13,
       demultiplexer_10_out0, demultiplexer_10_out1, demultiplexer_10_out2, demultiplexer_10_out3,
       demultiplexer_10_out4, demultiplexer_10_out5, demultiplexer_10_out10, demultiplexer_10_out11,
       demultiplexer_10_out12, demultiplexer_10_out13, demultiplexer_11_out0, demultiplexer_11_out2,
       demultiplexer_11_out3, demultiplexer_11_out4, demultiplexer_11_out5, demultiplexer_11_out8,
       demultiplexer_11_out15, demultiplexer_12_out8, demultiplexer_12_out15, demultiplexer_13_out8,
       demultiplexer_14_out6, demultiplexer_14_out8, demultiplexer_14_out9, demultiplexer_14_out10,
       demultiplexer_14_out11, demultiplexer_15_out0, demultiplexer_15_out1, demultiplexer_15_out3,
       demultiplexer_15_out4, demultiplexer_16_out1, demultiplexer_16_out2, EOD_ACT, ET1, ETO3, F_ACT,
       F_SINK, F_VAL, FLAG, FTIN_ACT, JUMP_ACT, JUMP_R_TOKEN_IN, JUMP_R_TOKEN_OUT, JUMP_SINK, LOAD_ACT,
       LOAD_SINK, multiplexer_13_out, multiplexer_14_out, multiplexer_16_out, NOJUMP_SINK, NOP_SINK,
       or_2_out, or_4_out, or_5_out, or_11_out, or_12_out, or_13_out, or_15_out, or_16_out, or_18_out,
       or_20_out, or_21_out, or_22_out, or_23_out, or_24_out, or_30_out, or_36_out, or_37_out, or_39_out,
       or_40_out, PRE_OUT, PT1, PT2, PT3, PTO1, PTO2, PTO3, register_4_q, register_5_q, register_16_q,
       registers_1_tout, sfeq, sfeqi, sfges, sfgesi, sfgeu, sfgeui, sfgts, sfgtsi, sfgtu, sfgtui, sfles,
       sflesi, sfleu, sfleui, sflts, sfltsi, sfltu, sfltui, sfne, sfnei, STORE_out, T1, TEOC, TOKEN_out,
       UP_ACT;
  wire [1:0] or_3_out, or_10_out;
  wire [2:0] or_6_out, or_17_out, register_3_q, WHERE_out;
  wire [2:1] demultiplexer_5_out7;
  wire [4:0] bitfinder_1_index, bitfinder_2_index, EA1, IMM_SHIFT, L5, multiplexer_2_out, multiplexer_5_out,
       register_6_q;
  wire [4:3] demultiplexer_5_out6;
  wire [31:0] add, adder_1_out, adder_6_out, addi, ALU_VAL, \and , andi, bit_extender_1_out,
       bit_extender_2_out, bit_extender_3_out, bit_extender_4_out, bit_extender_5_out, bit_extender_6_out,
       bit_extender_7_out, bit_extender_8_out, bit_extender_9_out, C0x2IR, div, divu, EBI1, EOD_VAL, ff1,
       fl1, IMM11S, IMM11Z, IMM26, IMM26S, IMMS, IMMZ, JUMP_ADDR, LOAD_REG_VAL, mul, muli, multiplexer_1_out,
       multiplexer_3_out, multiplexer_4_out, multiplexer_6_out, multiplexer_7_out, multiplexer_8_out,
       multiplexer_9_out, multiplexer_10_out, multiplexer_11_out, multiplexer_12_out, multiplexer_15_out,
       multiplexer_17_out, mulu, \or , ori, PB1, PB2, PB3, R1, R2, R3, register_7_q, registers_1_bout, ror,
       rori, shifter_1_out, shifter_9_out, sll, slli, sra, srai, srl, srli, sub, subtractor_2_out, \xor ,
       xori;
  wire [31:24] adder_2_out, adder_3_out, PC_OUT;

  D_Flip_Flop d_ff_1 (.clk(CLK), .D(FTIN_ACT), .Q(d_ff_1_q), .en(1'b1));  // open: Qn, preset, reset
  Comparator #(.width(32), .mode("unsigned")) comparator_1 (
    .a({32{1'b0}}), .b({PC_OUT, RAMIRADDR}), .gt(comparator_1_gt), .lt(comparator_1_lt));  // open: eq
  or or_1 (T1, d_ff_1_q, JUMP_SINK, TIN);
  or or_2 (or_2_out, comparator_1_gt, comparator_1_lt);
  D_Flip_Flop d_ff_2 (.clk(CLK), .D(FTIN), .Q(FTIN_ACT), .en(1'b1));  // open: Qn, preset, reset
  and and_1 (TRAMIROUT, T1, or_2_out);
  Adder #(.width(32)) adder_1 (.a(32'h4), .b({PC_OUT, RAMIRADDR}), .out(adder_1_out));  // open: cin, cout
  Multiplexer #(.select(2), .width(32)) multiplexer_1 (
    .in0(32'h2000), .in1(adder_1_out), .in2(EOD_VAL), .out(multiplexer_1_out), .sel(or_3_out), .en(1'b1));  // open: in3
  assign or_3_out = 2'b00 | {1'b0, UP_ACT} | {EOD_ACT, 1'b0};  // OR_Gate or_3, 2 bits wide
  or or_4 (or_4_out, FTIN_ACT, UP_ACT, EOD_ACT);
  Register #(.width(32)) IR (.D(RAMIRIN), .en(TRAMIRIN), .Q(C0x2IR), .clk(CLK), .clr(FTIN));
  Register #(.width(32)) PC (.D(multiplexer_1_out), .en(or_4_out), .Q({PC_OUT, RAMIRADDR}), .clk(CLK), .clr(FTIN));
  D_Flip_Flop d_ff_3 (.clk(CLK), .D(TRAMIRIN), .Q(UP_ACT), .en(1'b1));  // open: Qn, preset, reset
  Register #(.width(1)) F (.D(F_VAL), .en(F_ACT), .Q(FLAG), .clk(CLK), .clr(FTIN));
  D_Flip_Flop d_ff_4 (.clk(CLK), .D(d_ff_5_q), .Q(d_ff_4_q), .en(1'b1));  // open: Qn, preset, reset
  D_Flip_Flop d_ff_5 (.clk(CLK), .D(UP_ACT), .Q(d_ff_5_q), .en(1'b1));  // open: Qn, preset, reset
  Demultiplexer #(.select(2), .disabled(0)) demultiplexer_1 (
    .out0(C0x0T), .out1(C0x1T), .out2(C0x2T), .out3(C0x3T), .in(PRE_OUT), .sel(C0x2IR[31:30]), .en(PRE_OUT));
  Demultiplexer #(.select(4), .disabled(0)) demultiplexer_2 (
    .out1(demultiplexer_2_out1), .out2(demultiplexer_2_out2), .out3(demultiplexer_2_out3),
    .out4(demultiplexer_2_out4), .out5(demultiplexer_2_out5), .out6(demultiplexer_2_out6), .in(C0x2T),
    .sel(C0x2IR[29:26]), .en(C0x2T));  // open: out0, out7, out8, out9, out10, out11, out12, out13, out14, out15
  Register #(.width(5)) register_1 (.D(C0x2IR[4:0]), .en(d_ff_4_q), .Q(IMM_SHIFT), .clk(CLK));  // open: clr
  D_Flip_Flop d_ff_6 (.clk(CLK), .D(d_ff_4_q), .Q(PT1), .en(1'b1));  // open: Qn, preset, reset
  assign bit_extender_1_out = {{16{1'b0}}, C0x2IR[15:0]};  // Bit_Extender bit_extender_1
  assign bit_extender_2_out = {{16{C0x2IR[15]}}, C0x2IR[15:0]};  // Bit_Extender bit_extender_2
  or or_5 (or_5_out, demultiplexer_2_out3, demultiplexer_2_out1, demultiplexer_2_out2, demultiplexer_2_out4, demultiplexer_2_out5, demultiplexer_2_out6);
  Adder #(.width(32)) adder_2 (.a(IMMS), .b(R2), .out({adder_2_out, LOAD_ADDR}));  // open: cin, cout
  Register #(.width(32)) IMM_Z (.D(bit_extender_1_out), .en(d_ff_4_q), .Q(IMMZ), .clk(CLK));  // open: clr
  Register #(.width(32)) IMM_S (.D(bit_extender_2_out), .en(d_ff_4_q), .Q(IMMS), .clk(CLK));  // open: clr
  Register #(.width(32)) u_IMM26 (
    .D({PC_OUT[31:28], C0x2IR[25:0], 2'b00}), .en(d_ff_4_q), .Q(IMM26), .clk(CLK));  // open: clr
  assign bit_extender_3_out = {{4{C0x2IR[25]}}, {C0x2IR[25:0], 2'b00}};  // Bit_Extender bit_extender_3
  or or_6 (or_6_out[0], demultiplexer_2_out3, demultiplexer_2_out4);
  or or_7 (or_6_out[1], demultiplexer_2_out5, demultiplexer_2_out6);
  or or_8 (or_6_out[2], demultiplexer_2_out1, demultiplexer_2_out2);
  Register #(.width(32)) IMM26_2 (.D(bit_extender_3_out), .en(d_ff_4_q), .Q(IMM26S), .clk(CLK));  // open: clr
  Multiplexer #(.select(3), .width(5), .disabled(0)) multiplexer_2 (
    .in0(5'b01001), .in1(C0x2IR[25:21]), .in2(C0x2IR[20:16]), .in3(C0x2IR[15:11]), .in4(EA1),
    .out(multiplexer_2_out), .sel(WHERE_out), .en(TOKEN_out));  // open: in5, in6, in7
  Multiplexer #(.select(3), .width(32), .disabled(0)) multiplexer_3 (
    .in0({PC_OUT, RAMIRADDR}), .in1({32{1'b0}}), .in2({32{1'b0}}), .in3({32{1'b0}}), .in4(EBI1),
    .out(multiplexer_3_out), .sel(WHERE_out), .en(TOKEN_out));  // open: in5, in6, in7
  D_Flip_Flop d_ff_7 (.clk(CLK), .D(or_5_out), .Q(LOAD_TOKEN_OUT), .en(1'b1));  // open: Qn, preset, reset
  assign bit_extender_4_out = {{16{1'b0}}, {C0x2IR[25:21], C0x2IR[10:0]}};  // Bit_Extender bit_extender_4
  assign bit_extender_5_out = {{16{C0x2IR[25]}}, {C0x2IR[25:21], C0x2IR[10:0]}};  // Bit_Extender bit_extender_5
  assign WHERE_out = {2'b00, PT1} | {1'b0, PT2, 1'b0} | {1'b0, {2{PT3}}} | {ET1, 2'b00};  // OR_Gate WHERE, 3 bits wide
  or TOKEN (TOKEN_out, JUMP_R_TOKEN_OUT, PT1, PT2, PT3, ET1);
  or STORE (STORE_out, JUMP_R_TOKEN_OUT, 1'b0, 1'b0, 1'b0, ET1);
  Register #(.width(4)) register_2 (.D({1'b0, or_6_out}), .en(or_5_out), .Q(LOAD_BYTE_W), .clk(CLK));  // open: clr
  Register #(.width(32)) IMM11_Z (.D(bit_extender_4_out), .en(d_ff_4_q), .Q(IMM11Z), .clk(CLK));  // open: clr
  Register #(.width(32)) IMM11_Z_2 (.D(bit_extender_5_out), .en(d_ff_4_q), .Q(IMM11S), .clk(CLK));  // open: clr
  Register #(.width(5)) u_L5 (.D(C0x2IR[4:0]), .en(d_ff_4_q), .Q(L5), .clk(CLK));  // open: clr
  Register #(.width(3)) register_3 (.D(WHERE_out), .en(TOKEN_out), .Q(register_3_q), .clk(CLK));  // open: clr
  Register #(.width(1)) register_4 (.D(TOKEN_out), .en(1'b1), .Q(register_4_q), .clk(CLK));  // open: clr
  Register #(.width(1)) register_5 (.D(STORE_out), .en(TOKEN_out), .Q(register_5_q), .clk(CLK));  // open: clr
  Register #(.width(5)) register_6 (.D(multiplexer_2_out), .en(TOKEN_out), .Q(register_6_q), .clk(CLK));  // open: clr
  Register #(.width(32)) register_7 (.D(multiplexer_3_out), .en(TOKEN_out), .Q(register_7_q), .clk(CLK));  // open: clr
  Register #(.width(32)) _1_R (.D(PB1), .en(PTO1), .Q(R1), .clk(CLK));  // open: clr
  registers registers_1 (
    .CLEAR(FTIN), .CLK(CLK), .TIN(register_4_q), .STORE(register_5_q), .AIN(register_6_q),
    .BIN(register_7_q), .TOUT(registers_1_tout), .BOUT(registers_1_bout));
  D_Flip_Flop d_ff_8 (.clk(CLK), .D(PTO1), .Q(PT2), .en(1'b1));  // open: Qn, preset, reset
  Demultiplexer #(.select(3), .disabled(0)) demultiplexer_3 (
    .out0(JUMP_R_TOKEN_IN), .out1(PTO1), .out2(PTO2), .out3(PTO3), .out4(ETO3), .in(registers_1_tout),
    .sel(register_3_q), .en(registers_1_tout));  // open: out5, out6, out7
  Demultiplexer #(.select(3), .width(32), .disabled(0)) demultiplexer_4 (
    .out1(PB1), .out2(PB2), .out3(PB3), .in(registers_1_bout), .sel(register_3_q), .en(registers_1_tout));  // open: out0, out4, out5, out6, out7
  Register #(.width(32)) _2_R (.D(PB2), .en(PTO2), .Q(R2), .clk(CLK));  // open: clr
  D_Flip_Flop d_ff_9 (.clk(CLK), .D(LOAD_TOKEN_IN), .Q(LOAD_ACT), .en(1'b1));  // open: Qn, preset, reset
  Register #(.width(32)) _3_R (.D(PB3), .en(PTO3), .Q(R3), .clk(CLK));  // open: clr
  D_Flip_Flop d_ff_10 (.clk(CLK), .D(PTO2), .Q(PT3), .en(1'b1));  // open: Qn, preset, reset
  assign bit_extender_6_out = {{16{1'b0}}, LOAD_DATA[15:0]};  // Bit_Extender bit_extender_6
  assign bit_extender_7_out = {{16{LOAD_DATA[15]}}, LOAD_DATA[15:0]};  // Bit_Extender bit_extender_7
  assign bit_extender_8_out = {{24{1'b0}}, LOAD_DATA[7:0]};  // Bit_Extender bit_extender_8
  assign bit_extender_9_out = {{24{LOAD_DATA[7]}}, LOAD_DATA[7:0]};  // Bit_Extender bit_extender_9
  D_Flip_Flop d_ff_11 (.clk(CLK), .D(PTO3), .Q(PRE_OUT), .en(1'b1));  // open: Qn, preset, reset
  or or_9 (TEOC, LOAD_SINK, STORE_TOKEN_IN, NOJUMP_SINK, NOP_SINK, ALU_SINK, F_SINK);
  Multiplexer #(.select(4), .width(32)) multiplexer_4 (
    .in1(LOAD_DATA), .in2(LOAD_DATA), .in3(bit_extender_8_out), .in4(bit_extender_9_out),
    .in5(bit_extender_6_out), .in6(bit_extender_7_out), .out(multiplexer_4_out), .sel(C0x2IR[29:26]),
    .en(LOAD_TOKEN_IN));  // open: in0, in7, in8, in9, in10, in11, in12, in13, in14, in15
  Register #(.width(32)) register_8 (
    .D(multiplexer_4_out), .en(LOAD_TOKEN_IN), .Q(LOAD_REG_VAL), .clk(CLK));  // open: clr
  assign or_10_out = 2'b00 | {ALU_ACT, 1'b0};  // OR_Gate or_10, 2 bits wide
  Multiplexer #(.select(2), .width(5), .disabled(0)) multiplexer_5 (
    .in0(C0x2IR[25:21]), .in2(C0x2IR[25:21]), .out(multiplexer_5_out), .sel(or_10_out), .en(or_11_out));  // open: in1, in3
  Multiplexer #(.select(2), .width(32), .disabled(0)) multiplexer_6 (
    .in0(LOAD_REG_VAL), .in2(ALU_VAL), .out(multiplexer_6_out), .sel(or_10_out), .en(or_11_out));  // open: in1, in3
  or or_11 (or_11_out, LOAD_ACT, ALU_ACT);
  and and_2 (ET1, d_ff_14_q, d_ff_13_q);
  D_Flip_Flop d_ff_12 (.clk(CLK), .D(LOAD_ACT), .Q(LOAD_SINK), .en(1'b1));  // open: Qn, preset, reset
  D_Flip_Flop d_ff_13 (.clk(CLK), .D(TEOC), .Q(d_ff_13_q), .en(1'b1));  // open: Qn, preset, reset
  D_Flip_Flop d_ff_14 (.clk(CLK), .D(or_11_out), .Q(d_ff_14_q), .en(or_12_out));  // open: Qn, preset, reset
  or or_12 (or_12_out, or_11_out, or_13_out);
  Register #(.width(32)) register_9 (.D(multiplexer_6_out), .en(or_11_out), .Q(EBI1), .clk(CLK));  // open: clr
  Register #(.width(5)) register_10 (.D(multiplexer_5_out), .en(or_11_out), .Q(EA1), .clk(CLK));  // open: clr
  and and_3 (and_3_out, ~d_ff_14_q, d_ff_13_q);  // AND_Gate
  D_Flip_Flop d_ff_15 (.clk(CLK), .D(or_13_out), .Q(d_ff_15_q), .en(1'b1));  // open: Qn, preset, reset
  or or_13 (or_13_out, and_3_out, ETO3);
  Demultiplexer #(.select(4), .disabled(0)) demultiplexer_5 (
    .out5(demultiplexer_5_out7[2]), .out6(demultiplexer_5_out6[3]), .out7(demultiplexer_5_out7[1]),
    .in(C0x3T), .sel(C0x2IR[29:26]), .en(C0x3T));  // open: out0, out1, out2, out3, out4, out8, out9, out10, out11, out12, out13, out14, out15
  or or_14 (demultiplexer_5_out6[4], demultiplexer_5_out7[1], demultiplexer_5_out6[3]);
  or or_15 (or_15_out, JUMP_ACT, d_ff_15_q);
  D_Flip_Flop d_ff_16 (.clk(CLK), .D(d_ff_15_q), .Q(TOUT), .en(1'b1));  // open: Qn, preset, reset
  or or_16 (or_16_out, demultiplexer_5_out7[2], demultiplexer_5_out6[3], demultiplexer_5_out7[1]);
  Adder #(.width(32)) adder_3 (.a(R2), .b(IMM11S), .out({adder_3_out, STORE_ADDR}));  // open: cin, cout
  Shifter #(.width(32)) shifter_1 (.in(R3), .\dist ({demultiplexer_5_out6, 3'b000}), .out(shifter_1_out));
  D_Flip_Flop d_ff_17 (.clk(CLK), .D(JUMP_ACT), .Q(d_ff_17_q), .en(or_15_out));  // open: Qn, preset, reset
  Register #(.width(32)) register_11 (.D(JUMP_ADDR), .en(JUMP_ACT), .Q(EOD_VAL), .clk(CLK));  // open: clr
  Register #(.width(4)) register_12 (
    .D({1'b0, demultiplexer_5_out7, demultiplexer_5_out6[3]}), .en(or_16_out), .Q(STORE_BYTE_W), .clk(CLK));  // open: clr
  D_Flip_Flop d_ff_18 (.clk(CLK), .D(or_16_out), .Q(STORE_TOKEN_OUT), .en(1'b1));  // open: Qn, preset, reset
  Register #(.width(32)) register_13 (.D(shifter_1_out), .en(or_16_out), .Q(STORE_DATA), .clk(CLK));  // open: clr
  and and_4 (EOD_ACT, d_ff_17_q, d_ff_15_q);
  Demultiplexer #(.select(4), .disabled(0)) demultiplexer_6 (
    .out7(demultiplexer_6_out7), .out9(demultiplexer_6_out9), .out10(demultiplexer_6_out10),
    .out11(demultiplexer_6_out11), .out12(demultiplexer_6_out12), .out14(demultiplexer_6_out14),
    .out15(demultiplexer_6_out15), .in(C0x2T), .sel(C0x2IR[29:26]), .en(C0x2T));  // open: out0, out1, out2, out3, out4, out5, out6, out8, out13
  Demultiplexer #(.select(4), .disabled(0)) demultiplexer_7 (
    .out8(demultiplexer_7_out8), .out9(demultiplexer_7_out9), .in(C0x3T), .sel(C0x2IR[29:26]), .en(C0x3T));  // open: out0, out1, out2, out3, out4, out5, out6, out7, out10, out11, out12, out13, out14, out15
  Adder #(.width(32)) adder_4 (.a(IMMS), .b(R2), .out(addi));  // open: cin, cout
  assign xori = IMMS ^ R2;  // XOR_Gate xor_1, 32 bits wide
  Shifter #(.width(32)) shifter_2 (.in(R2), .\dist (L5), .out(slli));
  Demultiplexer #(.select(2), .disabled(0)) demultiplexer_8 (
    .out0(demultiplexer_8_out0), .out1(demultiplexer_8_out1), .out2(demultiplexer_8_out2),
    .out3(demultiplexer_8_out3), .in(demultiplexer_7_out8), .sel(C0x2IR[9:8]), .en(demultiplexer_7_out8));
  Adder #(.width(32)) adder_5 (.a(R3), .b(R2), .out(add));  // open: cin, cout
  BitFinder #(.width(32), .\type ("high1")) bitfinder_1 (.in(R2), .index(bitfinder_1_index));  // open: found
  Shifter #(.width(32)) shifter_3 (.in(R2), .\dist (R3[4:0]), .out(sll));
  or or_17 (or_17_out[0], demultiplexer_6_out7, demultiplexer_6_out9, demultiplexer_6_out10, demultiplexer_6_out11, demultiplexer_6_out12, demultiplexer_6_out14);
  assign fl1 = {{27{1'b0}}, bitfinder_1_index};  // Bit_Extender bit_extender_10
  Demultiplexer #(.select(5), .disabled(0)) demultiplexer_9 (
    .out0(demultiplexer_9_out0), .out1(demultiplexer_9_out1), .out2(demultiplexer_9_out2),
    .out3(demultiplexer_9_out3), .out4(demultiplexer_9_out4), .out5(demultiplexer_9_out5),
    .out10(demultiplexer_9_out10), .out11(demultiplexer_9_out11), .out12(demultiplexer_9_out12),
    .out13(demultiplexer_9_out13), .in(demultiplexer_6_out15), .sel(C0x2IR[25:21]), .en(demultiplexer_6_out15));  // open: out6, out7, out8, out9, out14, out15, out16, out17, out18, out19, out20, out21, out22, out23, out24, out25, out26, out27, out28, out29, out30, out31
  Demultiplexer #(.select(5), .disabled(0)) demultiplexer_10 (
    .out0(demultiplexer_10_out0), .out1(demultiplexer_10_out1), .out2(demultiplexer_10_out2),
    .out3(demultiplexer_10_out3), .out4(demultiplexer_10_out4), .out5(demultiplexer_10_out5),
    .out10(demultiplexer_10_out10), .out11(demultiplexer_10_out11), .out12(demultiplexer_10_out12),
    .out13(demultiplexer_10_out13), .in(demultiplexer_7_out9), .sel(C0x2IR[25:21]), .en(demultiplexer_7_out9));  // open: out6, out7, out8, out9, out14, out15, out16, out17, out18, out19, out20, out21, out22, out23, out24, out25, out26, out27, out28, out29, out30, out31
  assign andi = IMMZ & R2;  // AND_Gate and_5, 32 bits wide
  Multiplier #(.width(32)) multiplier_1 (.a(IMMZ), .b(R2), .out(muli));  // open: cin, cout
  Shifter #(.width(32), .shift("ar")) shifter_4 (.in(R2), .\dist (L5), .out(srai));
  Demultiplexer #(.select(4), .disabled(0)) demultiplexer_11 (
    .out0(demultiplexer_11_out0), .out2(demultiplexer_11_out2), .out3(demultiplexer_11_out3),
    .out4(demultiplexer_11_out4), .out5(demultiplexer_11_out5), .out8(demultiplexer_11_out8),
    .out15(demultiplexer_11_out15), .in(demultiplexer_8_out0), .sel(C0x2IR[3:0]), .en(demultiplexer_8_out0));  // open: out1, out6, out7, out9, out10, out11, out12, out13, out14
  Demultiplexer #(.select(4), .disabled(0)) demultiplexer_12 (
    .out8(demultiplexer_12_out8), .out15(demultiplexer_12_out15), .in(demultiplexer_8_out1),
    .sel(C0x2IR[3:0]), .en(demultiplexer_8_out1));  // open: out0, out1, out2, out3, out4, out5, out6, out7, out9, out10, out11, out12, out13, out14
  Demultiplexer #(.select(4), .disabled(0)) demultiplexer_13 (
    .out8(demultiplexer_13_out8), .in(demultiplexer_8_out2), .sel(C0x2IR[3:0]), .en(demultiplexer_8_out2));  // open: out0, out1, out2, out3, out4, out5, out6, out7, out9, out10, out11, out12, out13, out14, out15
  Demultiplexer #(.select(4), .disabled(0)) demultiplexer_14 (
    .out6(demultiplexer_14_out6), .out8(demultiplexer_14_out8), .out9(demultiplexer_14_out9),
    .out10(demultiplexer_14_out10), .out11(demultiplexer_14_out11), .in(demultiplexer_8_out3),
    .sel(C0x2IR[3:0]), .en(demultiplexer_8_out3));  // open: out0, out1, out2, out3, out4, out5, out7, out12, out13, out14, out15
  assign \and  = R3 & R2;  // AND_Gate and_6, 32 bits wide
  Multiplier #(.width(32)) multiplier_2 (.a(R3), .b(R2), .out(mul));  // open: cin, cout
  Shifter #(.width(32), .shift("lr")) shifter_5 (.in(R2), .\dist (R3[4:0]), .out(srl));
  Multiplexer #(.select(2), .width(32)) multiplexer_7 (
    .in0(slli), .in1(srli), .in2(srai), .in3(rori), .out(multiplexer_7_out), .sel(C0x2IR[7:6]),
    .en(or_17_out[0]));
  buf or_18 (or_18_out, 1'b0);  // OR_Gate
  Comparator #(.width(32), .mode("unsigned")) comparator_2 (.a(R2), .b(R3), .gt(sfgtu), .eq(sfeq), .lt(sfltu));
  Comparator #(.width(32), .mode("unsigned")) comparator_3 (.a(R2), .b(IMMS), .gt(sfgtui), .eq(sfeqi), .lt(sfltui));
  Demultiplexer #(.select(4), .disabled(0)) demultiplexer_15 (
    .out0(demultiplexer_15_out0), .out1(demultiplexer_15_out1), .out3(demultiplexer_15_out3),
    .out4(demultiplexer_15_out4), .out5(NOP_SINK), .in(C0x0T), .sel(C0x2IR[29:26]), .en(C0x0T));  // open: out2, out6, out7, out8, out9, out10, out11, out12, out13, out14, out15
  Demultiplexer #(.select(4), .disabled(0)) demultiplexer_16 (
    .out1(demultiplexer_16_out1), .out2(demultiplexer_16_out2), .in(C0x1T), .sel(C0x2IR[29:26]), .en(C0x1T));  // open: out0, out3, out4, out5, out6, out7, out8, out9, out10, out11, out12, out13, out14, out15
  assign ori = IMMZ | R2;  // OR_Gate or_19, 32 bits wide
  Shifter #(.width(32), .shift("rr")) shifter_6 (.in(R2), .\dist (L5), .out(rori));
  Shifter #(.width(32), .shift("lr")) shifter_7 (.in(R2), .\dist (L5), .out(srli));
  or or_20 (or_20_out, demultiplexer_11_out0, demultiplexer_11_out2, demultiplexer_11_out3, demultiplexer_11_out4, demultiplexer_11_out5, demultiplexer_11_out8, demultiplexer_11_out15, demultiplexer_12_out8);
  or or_21 (or_21_out, demultiplexer_12_out15, demultiplexer_13_out8, demultiplexer_14_out6);
  or or_22 (or_22_out, demultiplexer_14_out8, demultiplexer_14_out9, demultiplexer_14_out10, demultiplexer_14_out11);
  Divider #(.width(32)) divider_1 (.a(R2), .b(R3), .out(div));  // open: upper, rem
  Multiplier #(.width(32)) multiplier_3 (.a(R3), .b(R2), .out(mulu));  // open: cin, cout
  Shifter #(.width(32), .shift("ar")) shifter_8 (.in(R2), .\dist (R3[4:0]), .out(sra));
  or or_23 (or_23_out, demultiplexer_9_out0, demultiplexer_9_out1, demultiplexer_9_out2, demultiplexer_9_out3, demultiplexer_9_out4, demultiplexer_9_out5, demultiplexer_9_out10, demultiplexer_9_out11, demultiplexer_9_out12, demultiplexer_9_out13);
  or or_24 (or_24_out, demultiplexer_10_out0, demultiplexer_10_out1, demultiplexer_10_out2, demultiplexer_10_out3, demultiplexer_10_out4, demultiplexer_10_out5, demultiplexer_10_out10, demultiplexer_10_out11, demultiplexer_10_out12, demultiplexer_10_out13);
  or or_25 (sfgeu, sfeq, sfgtu);
  not not_1 (sfne, sfeq);
  or or_26 (sfleu, sfltu, sfeq);
  or or_27 (sfgeui, sfeqi, sfgtui);
  not not_2 (sfnei, sfeqi);
  or or_28 (sfleui, sfltui, sfeqi);
  or or_29 (or_17_out[2], or_20_out, or_21_out, or_22_out);
  or or_30 (or_30_out, or_23_out, or_24_out, or_18_out);
  Multiplexer #(.select(4), .width(32), .disabled(0)) multiplexer_8 (
    .in7(addi), .in9(andi), .in10(ori), .in11(xori), .in12(muli), .in14(multiplexer_7_out),
    .out(multiplexer_8_out), .sel(C0x2IR[29:26]), .en(or_17_out[0]));  // open: in0, in1, in2, in3, in4, in5, in6, in8, in13, in15
  Demultiplexer #(.select(4), .disabled(0)) demultiplexer_17 (
    .out6(or_17_out[1]), .in(C0x0T), .sel(C0x2IR[29:26]), .en(C0x0T));  // open: out0, out1, out2, out3, out4, out5, out7, out8, out9, out10, out11, out12, out13, out14, out15
  Divider #(.width(32)) divider_2 (.a(R2), .b(R3), .out(divu));  // open: upper, rem
  assign \or  = R3 | R2;  // OR_Gate or_31, 32 bits wide
  Subtractor #(.width(32)) subtractor_1 (.a(R2), .b(R3), .out(sub));  // open: bin, bout
  Comparator #(.width(32)) comparator_4 (.a(R2), .b(R3), .gt(sfgts), .eq(comparator_4_eq), .lt(sflts));
  Comparator #(.width(32)) comparator_5 (.a(R2), .b(IMMS), .gt(sfgtsi), .eq(comparator_5_eq), .lt(sfltsi));
  or or_32 (sfges, comparator_4_eq, sfgts);
  or or_33 (sfles, sflts, comparator_4_eq);
  or or_34 (sfgesi, comparator_5_eq, sfgtsi);
  or or_35 (sflesi, sfltsi, comparator_5_eq);
  or or_36 (or_36_out, demultiplexer_15_out4, demultiplexer_15_out3);
  or or_37 (or_37_out, and_7_out, and_8_out);
  and and_7 (and_7_out, ~FLAG, demultiplexer_15_out3);  // AND_Gate
  and and_8 (and_8_out, FLAG, demultiplexer_15_out4);
  Shifter #(.width(32)) shifter_9 (.in(IMMZ), .\dist (5'b10000), .out(shifter_9_out));
  Multiplexer #(.select(4), .width(32), .disabled(0)) multiplexer_9 (
    .in0(add), .in2(sub), .in3(\and ), .in4(\or ), .in5(\xor ), .in8(sll), .in15(ff1),
    .out(multiplexer_9_out), .sel(C0x2IR[3:0]), .en(or_17_out[2]));  // open: in1, in6, in7, in9, in10, in11, in12, in13, in14
  Multiplexer #(.select(4), .width(32), .disabled(0)) multiplexer_10 (
    .in8(srl), .in15(fl1), .out(multiplexer_10_out), .sel(C0x2IR[3:0]), .en(or_17_out[2]));  // open: in0, in1, in2, in3, in4, in5, in6, in7, in9, in10, in11, in12, in13, in14
  Multiplexer #(.select(4), .width(32), .disabled(0)) multiplexer_11 (
    .in8(sra), .out(multiplexer_11_out), .sel(C0x2IR[3:0]), .en(or_17_out[2]));  // open: in0, in1, in2, in3, in4, in5, in6, in7, in9, in10, in11, in12, in13, in14, in15
  Multiplexer #(.select(4), .width(32), .disabled(0)) multiplexer_12 (
    .in6(mul), .in8(ror), .in9(div), .in10(divu), .in11(mulu), .out(multiplexer_12_out), .sel(C0x2IR[3:0]),
    .en(or_17_out[2]));  // open: in0, in1, in2, in3, in4, in5, in7, in12, in13, in14, in15
  BitFinder #(.width(32)) bitfinder_2 (.in(R2), .index(bitfinder_2_index));  // open: found
  assign ff1 = {{27{1'b0}}, bitfinder_2_index};  // Bit_Extender bit_extender_11
  Shifter #(.width(32), .shift("rr")) shifter_10 (.in(R2), .\dist (R3[4:0]), .out(ror));
  assign \xor  = R2 ^ R3;  // XOR_Gate xor_2, 32 bits wide
  Multiplexer #(.select(5), .disabled(0)) multiplexer_13 (
    .in0(sfeqi), .in1(sfnei), .in2(sfgtui), .in3(sfgeui), .in4(sfltui), .in5(sfleui), .in10(sfgtsi),
    .in11(sfgesi), .in12(sfltsi), .in13(sflesi), .out(multiplexer_13_out), .sel(C0x2IR[25:21]), .en(or_30_out));  // open: in6, in7, in8, in9, in14, in15, in16, in17, in18, in19, in20, in21, in22, in23, in24, in25, in26, in27, in28, in29, in30, in31
  Multiplexer #(.select(5), .disabled(0)) multiplexer_14 (
    .in0(sfeq), .in1(sfne), .in2(sfgtu), .in3(sfgeu), .in4(sfltu), .in5(sfleu), .in10(sfgts), .in11(sfges),
    .in12(sflts), .in13(sfles), .out(multiplexer_14_out), .sel(C0x2IR[25:21]), .en(or_30_out));  // open: in6, in7, in8, in9, in14, in15, in16, in17, in18, in19, in20, in21, in22, in23, in24, in25, in26, in27, in28, in29, in30, in31
  and and_9 (NOJUMP_SINK, or_36_out, ~or_37_out);  // AND_Gate
  or or_38 (JUMP_ACT, and_7_out, and_8_out, demultiplexer_15_out0, demultiplexer_15_out1, demultiplexer_16_out1, demultiplexer_16_out2);
  Multiplexer #(.select(2), .width(32), .disabled(0)) multiplexer_15 (
    .in0(multiplexer_9_out), .in1(multiplexer_10_out), .in2(multiplexer_11_out), .in3(multiplexer_12_out),
    .out(multiplexer_15_out), .sel(C0x2IR[9:8]), .en(or_17_out[2]));
  Multiplexer #(.disabled(0)) multiplexer_16 (
    .in0(multiplexer_13_out), .in1(multiplexer_14_out), .out(multiplexer_16_out), .sel(demultiplexer_7_out9),
    .en(or_30_out));
  Register #(.width(1)) register_14 (.D(multiplexer_16_out), .en(or_30_out), .Q(F_VAL), .clk(CLK));  // open: clr
  D_Flip_Flop d_ff_19 (.clk(CLK), .D(or_30_out), .Q(F_ACT), .en(1'b1));  // open: Qn, preset, reset
  Adder #(.width(32)) adder_6 (.a(IMM26S), .b({PC_OUT, RAMIRADDR}), .out(adder_6_out));  // open: cin, cout
  Multiplexer #(.select(3), .width(32), .disabled(0)) multiplexer_17 (
    .in1(multiplexer_8_out), .in2(shifter_9_out), .in4(multiplexer_15_out), .out(multiplexer_17_out),
    .sel(or_17_out), .en(or_39_out));  // open: in0, in3, in5, in6, in7
  or or_39 (or_39_out, or_17_out[1], or_17_out[0], or_17_out[2]);
  Subtractor #(.width(32)) subtractor_2 (.a(adder_6_out), .b(32'h4), .out(subtractor_2_out));  // open: bin, bout
  Multiplexer #(.width(32), .disabled(0)) multiplexer_18 (
    .in0(subtractor_2_out), .in1(R3), .out(JUMP_ADDR), .sel(C0x2IR[30]), .en(JUMP_ACT));
  or or_40 (or_40_out, demultiplexer_16_out2, demultiplexer_15_out1);
  Register #(.width(32)) register_15 (.D(multiplexer_17_out), .en(or_39_out), .Q(ALU_VAL), .clk(CLK));  // open: clr
  D_Flip_Flop d_ff_20 (.clk(CLK), .D(or_39_out), .Q(ALU_ACT), .en(1'b1));  // open: Qn, preset, reset
  D_Flip_Flop d_ff_21 (.clk(CLK), .D(ALU_ACT), .Q(ALU_SINK), .en(1'b1));  // open: Qn, preset, reset
  D_Flip_Flop d_ff_22 (.clk(CLK), .D(F_ACT), .Q(F_SINK), .en(1'b1));  // open: Qn, preset, reset
  D_Flip_Flop d_ff_23 (.clk(CLK), .D(JUMP_ACT), .Q(d_ff_23_q), .en(1'b1));  // open: Qn, preset, reset
  Register #(.width(1)) register_16 (.D(or_40_out), .en(JUMP_ACT), .Q(register_16_q), .clk(CLK));  // open: clr
  and and_10 (JUMP_R_TOKEN_OUT, d_ff_23_q, register_16_q);
  and and_11 (and_11_out, d_ff_23_q, ~register_16_q);  // AND_Gate
  D_Flip_Flop d_ff_24 (.clk(CLK), .D(JUMP_R_TOKEN_IN), .Q(d_ff_24_q), .en(1'b1));  // open: Qn, preset, reset
  or or_41 (JUMP_SINK, d_ff_24_q, and_11_out);

  // Other names for the same wires on the sheet: IR[31:0] = C0x2IR; PA3[4:0] = C0x2IR[15:11];
  //   PA2[4:0] = C0x2IR[20:16]; ALU_C[1] = ALU_ACT; EOD_ADD[1] = EOD_ACT; EW1[2] = ET1; IRA = TRAMIRIN;
  //   IRT[31:0] = RAMIRIN; LOAD_REG_ADDR[4:0] = C0x2IR[25:21]; PA1[4:0] = C0x2IR[25:21]; PW1[0] = PT1; PW2[1] = PT2;
  //   PW3[1:0] = {2{PT3}}; R35[4:0] = R3[4:0]; PC_OUT[23:0] = RAMIRADDR; EOC_CLK = CLK; LOAD_CLK = CLK; PCLK = CLK;
  //   RCLK = CLK; RINIT = FTIN; STORE_SINK = STORE_TOKEN_IN; UP_ADD[0] = UP_ACT

  // Notes on the sheet:
  //   TOKEN
  //   PRELOAD
  //   LOAD ZONE
  //   REGISTERS ZONE
  //   WRITE-REG
  //   WRITE-PC
  //   EOC ZONE
  //   STORE ZONE
  //   l.j 0000
  //   l.jal 0001
  //   l.bf 0100
  //   l.bnf 0011
  //   l.jalr 0010
  //   l.jr 0001
  //   imm
  //   reg
  //   ALU ZONE
  //   JUMP ZONE
endmodule

// GEN-R
module registers (
  input  CLEAR,
  input  CLK,
  input  TIN,
  input  STORE,
  input  [4:0] AIN,
  input  [31:0] BIN,
  output TOUT,
  output [31:0] BOUT
);

  wire and_1_out, s0, s1, s2, s3, s4, s5, s6, s7, s8, s9, s10, s11, s12, s13, s14, s15, s16, s17, s18, s19,
       s20, s21, s22, s23, s24, s25, s26, s27, s28, s29, s30, s31;
  wire [31:0] d0, d1, d2, d3, d4, d5, d6, d7, d8, d9, d10, d11, d12, d13, d14, d15, d16, d17, d18, d19, d20,
       d21, d22, d23, d24, d25, d26, d27, d28, d29, d30, d31, multiplexer_1_out, o0, o1, o2, o3, o4, o5, o6,
       o7, o8, o9, o10, o11, o12, o13, o14, o15, o16, o17, o18, o19, o20, o21, o22, o23, o24, o25, o26, o27,
       o28, o29, o30, o31;

  and and_1 (and_1_out, TIN, STORE);
  Decoder #(.select(5), .disabled(0)) decoder_1 (
    .out0(s0), .out1(s1), .out2(s2), .out3(s3), .out4(s4), .out5(s5), .out6(s6), .out7(s7), .out8(s8),
    .out9(s9), .out10(s10), .out11(s11), .out12(s12), .out13(s13), .out14(s14), .out15(s15), .out16(s16),
    .out17(s17), .out18(s18), .out19(s19), .out20(s20), .out21(s21), .out22(s22), .out23(s23), .out24(s24),
    .out25(s25), .out26(s26), .out27(s27), .out28(s28), .out29(s29), .out30(s30), .out31(s31), .sel(AIN),
    .en(and_1_out));
  Demultiplexer #(.select(5), .width(32), .disabled(0)) demultiplexer_1 (
    .out0(d0), .out1(d1), .out2(d2), .out3(d3), .out4(d4), .out5(d5), .out6(d6), .out7(d7), .out8(d8),
    .out9(d9), .out10(d10), .out11(d11), .out12(d12), .out13(d13), .out14(d14), .out15(d15), .out16(d16),
    .out17(d17), .out18(d18), .out19(d19), .out20(d20), .out21(d21), .out22(d22), .out23(d23), .out24(d24),
    .out25(d25), .out26(d26), .out27(d27), .out28(d28), .out29(d29), .out30(d30), .out31(d31), .in(BIN),
    .sel(AIN), .en(TIN));
  Register #(.width(32)) register_1 (.D(d0), .en(s0), .Q(o0), .clk(CLK), .clr(CLEAR));
  Register #(.width(32)) register_2 (.D(d4), .en(s4), .Q(o4), .clk(CLK), .clr(CLEAR));
  Register #(.width(32)) register_3 (.D(d8), .en(s8), .Q(o8), .clk(CLK), .clr(CLEAR));
  Register #(.width(32)) register_4 (.D(d12), .en(s12), .Q(o12), .clk(CLK), .clr(CLEAR));
  Register #(.width(32)) register_5 (.D(d16), .en(s16), .Q(o16), .clk(CLK), .clr(CLEAR));
  Register #(.width(32)) register_6 (.D(d20), .en(s20), .Q(o20), .clk(CLK), .clr(CLEAR));
  Register #(.width(32)) register_7 (.D(d24), .en(s24), .Q(o24), .clk(CLK), .clr(CLEAR));
  Register #(.width(32)) register_8 (.D(d28), .en(s28), .Q(o28), .clk(CLK), .clr(CLEAR));
  Register #(.width(32)) register_9 (.D(d1), .en(s1), .Q(o1), .clk(CLK), .clr(CLEAR));
  Register #(.width(32)) register_10 (.D(d5), .en(s5), .Q(o5), .clk(CLK), .clr(CLEAR));
  Register #(.width(32)) register_11 (.D(d9), .en(s9), .Q(o9), .clk(CLK), .clr(CLEAR));
  Register #(.width(32)) register_12 (.D(d13), .en(s13), .Q(o13), .clk(CLK), .clr(CLEAR));
  Register #(.width(32)) register_13 (.D(d17), .en(s17), .Q(o17), .clk(CLK), .clr(CLEAR));
  Register #(.width(32)) register_14 (.D(d21), .en(s21), .Q(o21), .clk(CLK), .clr(CLEAR));
  Register #(.width(32)) register_15 (.D(d25), .en(s25), .Q(o25), .clk(CLK), .clr(CLEAR));
  Register #(.width(32)) register_16 (.D(d29), .en(s29), .Q(o29), .clk(CLK), .clr(CLEAR));
  Register #(.width(32)) register_17 (.D(d2), .en(s2), .Q(o2), .clk(CLK), .clr(CLEAR));
  Register #(.width(32)) register_18 (.D(d6), .en(s6), .Q(o6), .clk(CLK), .clr(CLEAR));
  Register #(.width(32)) register_19 (.D(d10), .en(s10), .Q(o10), .clk(CLK), .clr(CLEAR));
  Register #(.width(32)) register_20 (.D(d14), .en(s14), .Q(o14), .clk(CLK), .clr(CLEAR));
  Register #(.width(32)) register_21 (.D(d18), .en(s18), .Q(o18), .clk(CLK), .clr(CLEAR));
  Register #(.width(32)) register_22 (.D(d22), .en(s22), .Q(o22), .clk(CLK), .clr(CLEAR));
  Register #(.width(32)) register_23 (.D(d26), .en(s26), .Q(o26), .clk(CLK), .clr(CLEAR));
  Register #(.width(32)) register_24 (.D(d30), .en(s30), .Q(o30), .clk(CLK), .clr(CLEAR));
  Register #(.width(32)) register_25 (.D(d3), .en(s3), .Q(o3), .clk(CLK), .clr(CLEAR));
  Register #(.width(32)) register_26 (.D(d7), .en(s7), .Q(o7), .clk(CLK), .clr(CLEAR));
  Register #(.width(32)) register_27 (.D(d11), .en(s11), .Q(o11), .clk(CLK), .clr(CLEAR));
  Register #(.width(32)) register_28 (.D(d15), .en(s15), .Q(o15), .clk(CLK), .clr(CLEAR));
  Register #(.width(32)) register_29 (.D(d19), .en(s19), .Q(o19), .clk(CLK), .clr(CLEAR));
  Register #(.width(32)) register_30 (.D(d23), .en(s23), .Q(o23), .clk(CLK), .clr(CLEAR));
  Register #(.width(32)) register_31 (.D(d27), .en(s27), .Q(o27), .clk(CLK), .clr(CLEAR));
  Register #(.width(32)) register_32 (.D(d31), .en(s31), .Q(o31), .clk(CLK), .clr(CLEAR));
  Multiplexer #(.select(5), .width(32)) multiplexer_1 (
    .in0(o0), .in1(o1), .in2(o2), .in3(o3), .in4(o4), .in5(o5), .in6(o6), .in7(o7), .in8(o8), .in9(o9),
    .in10(o10), .in11(o11), .in12(o12), .in13(o13), .in14(o14), .in15(o15), .in16(o16), .in17(o17),
    .in18(o18), .in19(o19), .in20(o20), .in21(o21), .in22(o22), .in23(o23), .in24(o24), .in25(o25),
    .in26(o26), .in27(o27), .in28(o28), .in29(o29), .in30(o30), .in31(o31), .out(multiplexer_1_out),
    .sel(AIN), .en(TIN));
  D_Flip_Flop d_ff_1 (.clk(CLK), .D(TIN), .Q(TOUT), .en(1'b1), .reset(CLEAR));  // open: Qn, preset
  Register #(.width(32)) register_33 (.D(multiplexer_1_out), .en(TIN), .Q(BOUT), .clk(CLK), .clr(CLEAR));

  // Other names for the same wires on the sheet: T = TIN
endmodule
