// Logisim project ram.circ as structural Verilog: 1 circuit, main circuit main
// RAM
module main (
  input  CLEAR,
  input  TIN,
  input  [31:0] BITS_IN,
  input  [23:0] ADDRESS,
  input  STORE,
  input  [3:0] BYTE_OPSIZE,
  input  CLK,
  output TOUT,
  output [31:0] BITS_OUT
);

  wire and_1_out, comparator_1_lt, d_ff_1_q, d_ff_2_q, d_ff_3_q, d_ff_4_q, d_ff_5_q, not_1_out, or_1_out;
  wire [3:0] counter_1_q;
  wire [7:0] multiplexer_2_out, ram_1_data, register_6_q, register_6_q_2;
  wire [23:0] adder_1_out, adder_2_out, adder_3_out, multiplexer_1_out, register_1_q, register_2_q,
       register_3_q;
  wire [31:16] register_6_q_3;

  Counter #(.width(4), .max('hf)) counter_1 (
    .Q(counter_1_q), .clk(and_1_out), .clr(TIN));  // open: load, D, count, carry
  and and_1 (and_1_out, or_1_out, CLK);
  Register #(.width(24)) register_1 (.D(ADDRESS), .en(1'b1), .Q(register_1_q), .clk(CLK));  // open: clr
  D_Flip_Flop d_ff_1 (.clk(CLK), .D(TIN), .Q(d_ff_1_q), .en(1'b1));  // open: Qn, preset, reset
  or or_1 (or_1_out, d_ff_1_q, d_ff_2_q, d_ff_3_q, d_ff_4_q);
  Adder #(.width(24)) adder_1 (.a(24'h1), .b(register_1_q), .out(adder_1_out));  // open: cin, cout
  D_Flip_Flop d_ff_2 (.clk(CLK), .D(d_ff_1_q), .Q(d_ff_2_q), .en(1'b1));  // open: Qn, preset, reset
  Comparator #(.width(4)) comparator_1 (.a(counter_1_q), .b(BYTE_OPSIZE), .lt(comparator_1_lt));  // open: gt, eq
  Register #(.width(24)) register_2 (.D(adder_1_out), .en(1'b1), .Q(register_2_q), .clk(CLK));  // open: clr
  Adder #(.width(24)) adder_2 (.a(24'h1), .b(register_2_q), .out(adder_2_out));  // open: cin, cout
  D_Flip_Flop d_ff_3 (.clk(CLK), .D(d_ff_2_q), .Q(d_ff_3_q), .en(1'b1));  // open: Qn, preset, reset
  Multiplexer #(.select(2), .width(24)) multiplexer_1 (
    .in0(ADDRESS), .in1(adder_1_out), .in2(adder_2_out), .in3(adder_3_out), .out(multiplexer_1_out),
    .sel(counter_1_q[1:0]), .en(1'b1));
  Register #(.width(24)) register_3 (.D(adder_2_out), .en(1'b1), .Q(register_3_q), .clk(CLK));  // open: clr
  Multiplexer #(.select(2), .width(8)) multiplexer_2 (
    .in0(BITS_IN[31:24]), .in1(BITS_IN[23:16]), .in2(BITS_IN[15:8]), .in3(BITS_IN[7:0]),
    .out(multiplexer_2_out), .sel(counter_1_q[1:0]), .en(1'b1));
  Register #(.width(24)) register_4 (.D(adder_3_out), .en(1'b1), .clk(CLK));  // open: Q, clr
  Adder #(.width(24)) adder_3 (.a(24'h1), .b(register_3_q), .out(adder_3_out));  // open: cin, cout
  D_Flip_Flop d_ff_4 (.clk(CLK), .D(d_ff_3_q), .Q(d_ff_4_q), .en(1'b1));  // open: Qn, preset, reset
  RAM #(.addrWidth(24), .bus("separate")) ram_1 (
    .addr(multiplexer_1_out), .din(multiplexer_2_out), .data(ram_1_data), .str(STORE), .sel(comparator_1_lt),
    .clk(CLK), .ld(not_1_out), .clr(CLEAR));
  not not_1 (not_1_out, STORE);
  D_Flip_Flop d_ff_5 (.clk(CLK), .D(d_ff_4_q), .Q(d_ff_5_q), .en(1'b1));  // open: Qn, preset, reset
  D_Flip_Flop d_ff_6 (.clk(CLK), .D(d_ff_5_q), .Q(TOUT), .en(1'b1));  // open: Qn, preset, reset
  Register #(.width(32)) register_5 (
    .D({register_6_q_3, register_6_q_2, register_6_q}), .en(d_ff_5_q), .Q(BITS_OUT), .clk(CLK));  // open: clr
  Register #(.width(32)) register_6 (
    .D({register_6_q_3[23:16], register_6_q_2, register_6_q, ram_1_data}), .en(1'b1),
    .Q({register_6_q_3, register_6_q_2, register_6_q}), .clk(CLK));  // open: clr
endmodule
