// Logisim project main.circ as structural Verilog: 2 circuits, main circuit main
module main (
);

  wire cpu_1_keyboard_purge, cpu_1_powered, cpu_1_running, cpu_1_tty_output, keyboard_1_avail, P_out;
  wire [6:0] cpu_1_tty_ascii, keyboard_1_data;
  wire [23:0] cpu_1_rom_addr;
  wire [31:0] rom_1_data;

  cpu cpu_1 (
    .ACTIVATE(P_out), .POWERED(cpu_1_powered), .ROM_DATA(rom_1_data), .RUNNING(cpu_1_running),
    .ROM_ADDR(cpu_1_rom_addr), .TTY_ASCII(cpu_1_tty_ascii), .TTY_OUTPUT(cpu_1_tty_output),
    .KEYBOARD_READ(keyboard_1_data), .KETBOARD_AVAL(keyboard_1_avail), .KEYBOARD_PURGE(cpu_1_keyboard_purge));
  ROM #(.addrWidth(24), .dataWidth(32)) rom_1 (.addr(cpu_1_rom_addr), .data(rom_1_data));  // open: sel
  LED RUNNING (.in(cpu_1_running));
  LED POWER (.in(cpu_1_powered));
  Button P (.out(P_out));
  TTY #(.rows(24), .cols(80)) tty_1 (.data(cpu_1_tty_ascii), .clk(cpu_1_tty_output));  // open: we, clr
  Keyboard #(.buflen(256)) keyboard_1 (
    .clk(cpu_1_keyboard_purge), .avail(keyboard_1_avail), .data(keyboard_1_data));  // open: re, clr

  // Notes on the sheet:
  //   contents of rom_1 (hex, n*v repeats v):
  //   2e48 7f454c46 1020100 0 0 2005c 1 100 34 2d08 0 340020 20028 80005 1 2000 0 0 a88 a88 5 2000 1 2a88
  //   2a88 2a88 4 4 6 2000 2019*0 d7e117f8 9c410000 d7e14ffc 9c21ffc0 1860496e a8637075 d7e21fd0 18607420
  //   a8637665 d7e21fd4 18606374 a8636f72 d7e21fd8 18603a20 a8632000 d7e21fdc 1860536f a8637274 d7e21fc0
  //   18606564 a8632076 d7e21fc4 18606563 a863746f d7e21fc8 1860723a a8632000 d7e21fcc 9c62ffd0 400019c
  //   15000000 18600020 d7e21fe8 8462ffe8 9c800001 40001fb 15000000 18600030 d7e21fe4 8462ffe8 8482ffe4
  //   40000ef 15000000 d7e25fe0 8462ffe0 d7e21ff4 9c62ffc0 400018a 15000000 9c600000 d7e21ff0 9 15000000
  //   8462ffe4 8482fff0 40000ac 15000000 8462fff0 9c630001 d7e21ff0 8482fff0 8462ffe0 e4841800 13fffff6
  //   15000000 9c600000 d7e21fec 1e 15000000 8462fff4 9c63ffff d7e21ff4 8462fff4 b8630002 8482ffe4
  //   e0841800 8462ffe4 4000118 15000000 8462fff4 b8630002 8482ffe4 e0641800 84630000 4000182 15000000
  //   9c600020 4000157 15000000 8462ffe4 8482fff4 9ca00000 4000014 15000000 8462ffec 9c630001 d7e21fec
  //   8482ffec 8462ffe0 e4841800 13ffffe1 15000000 9c60000a 4000147 15000000 9c600000 a9630000 a8220000
  //   8441fff8 8521fffc 44004800 15000000 d7e117f8 9c410000 d7e14ffc 9c21ffe8 d7e21ff0 d7e227ec d7e22fe8
  //   8462ffe8 e0631800 9c830001 8462ffec e4841800 10000004 15000000 60 15000000 8462ffe8 9c630001
  //   e0631800 a8830000 8462ffec e4841800 10000025 15000000 8462ffe8 b8630002 8482fff0 e0641800 84830000
  //   8462ffe8 b8630003 9c630004 84a2fff0 e0651800 84630000 e4a41800 10000015 15000000 8462ffe8 b8630002
  //   8482fff0 e0a41800 8462ffe8 b8630003 9c630004 8482fff0 e0841800 a8650000 40000c5 15000000 8462ffe8
  //   e0631800 9ca30001 8462fff0 8482ffec 7ffffc9 15000000 35 15000000 8462ffe8 e0631800 9c630001 d7e21ff4
  //   8462ffe8 9c630001 b8630003 8482fff0 e0641800 84830000 8462ffe8 b8630003 9c630004 84a2fff0 e0651800
  //   84630000 e4641800 10000005 15000000 8462fff4 9c630001 d7e21ff4 8462ffe8 b8630002 8482fff0 e0641800
  //   84830000 8462fff4 b8630002 84a2fff0 e0651800 84630000 e4a41800 10000012 15000000 8462ffe8 b8630002
  //   8482fff0 e0a41800 8462fff4 b8630002 8482fff0 e0841800 a8650000 400008e 15000000 8462fff0 8482ffec
  //   84a2fff4 7ffff94 15000000 a8220000 8441fff8 8521fffc 44004800 15000000 d7e117f8 9c410000 d7e14ffc
  //   9c21fff0 d7e21ff4 d7e227f0 8462fff0 bc230000 10000004 15000000 26 15000000 8462fff0 9c63ffff
  //   b8630041 b8630002 8482fff4 e0641800 84830000 8462fff0 b8630002 84a2fff4 e0651800 84630000 e4441800
  //   10000004 15000000 15 15000000 8462fff0 b8630002 8482fff4 e0a41800 8462fff0 9c63ffff b8630041
  //   b8630002 8482fff4 e0841800 a8650000 400005a 15000000 8462fff0 9c63ffff b8830041 8462fff4 7ffffd2
  //   15000000 a8220000 8441fff8 8521fffc 44004800 15000000 d7e117fc 9c410000 9c21ffe8 d7e21fec d7e227e8
  //   9c600000 d7e21ff8 9c600000 d7e21ff4 9c600000 d7e21ff0 2d 15000000 8482ffec 8462fff0 e0641800
  //   90630000 bda3002f 10000019 15000000 8482ffec 8462fff0 e0641800 90630000 bd430039 10000012 15000000
  //   8462fff8 e0631800 b8830002 e0632000 d7e21ff8 8482ffec 8462fff0 e0641800 90630000 a8830000 8462fff8
  //   e0641800 9c63ffd0 d7e21ff8 c 15000000 8462fff4 9c830001 d7e227f4 b8630002 8482ffe8 e0641800 8482fff8
  //   d4032000 9c600000 d7e21ff8 8462fff0 9c630001 d7e21ff0 8482ffec 8462fff0 e0641800 90630000 bc230000
  //   13ffffd0 15000000 8462fff4 9c830001 d7e227f4 b8630002 8482ffe8 e0641800 8482fff8 d4032000 8462fff4
  //   a9630000 a8220000 8441fffc 44004800 15000000 d7e117fc 9c410000 9c21fff4 d7e21ff8 d7e227f4 8482fff8
  //   8462fff4 e4241800 10000004 15000000 17 15000000 8462fff8 84830000 8462fff4 84630000 e0841805
  //   8462fff8 d4032000 8462fff4 84830000 8462fff8 84630000 e0841805 8462fff4 d4032000 8462fff8 84830000
  //   8462fff4 84630000 e0841805 8462fff8 d4032000 a8220000 8441fffc 44004800 15000000 d7e117fc 9c410000
  //   9c21fff0 d7e21ff4 d7e227f0 8462fff4 8482fff0 e063230a d7e21ff8 8462fff8 a9630000 a8220000 8441fffc
  //   44004800 15000000 d7e117f8 9c410000 d7e14ffc 9c21fff0 d7e21ff4 d7e227f0 8462fff4 8482fff0 7ffffe9
  //   15000000 a88b0000 8462fff0 e0641b06 8482fff4 e0641802 a9630000 a8220000 8441fff8 8521fffc 44004800
  //   15000000 d7e117fc 9c410000 9c21fff8 dbe21ff8 18600010 8c82fff8 d8032000 a8220000 844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
endmodule

// or1k - PC
module cpu (
  input  ACTIVATE,
  input  [31:0] ROM_DATA,
  input  KETBOARD_AVAL,
  input  [6:0] KEYBOARD_READ,
  output POWERED,
  output [23:0] ROM_ADDR,
  output RUNNING,
  output TTY_OUTPUT,
  output [6:0] TTY_ASCII,
  output KEYBOARD_PURGE
);

  wire and_1_out, and_2_out, and_3_out, CLEAR_TOKEN_OUT, CLK, comparator_1_lt, d_ff_1_q, d_ff_2_q, d_ff_4_q,
       d_ff_5_q, d_ff_6_q, d_ff_7_q, d_ff_10_q, d_ff_12_q, INIT_CYCLE, INIT_TOKEN_IN, INIT_TOKEN_OUT,
       IR_TOKEN_OUT, LOAD_TOKEN_OUT, main_1_tout, multiplexer_4_out, or1k___CPU_tout, or_1_out, or_2_out,
       or_3_out, or_4_out, or_5_out, or_7_out, or_8_out, STORE_TOKEN_OUT, TTY_TOKEN_OUT;
  wire [0:0] IR_SEL_IN;
  wire [1:1] LOAD_SEL_IN, STORE_SEL_IN;
  wire [2:2] KEY_SEL_IN, TTY_SEL_IN;
  wire [3:0] LOAD_BYTE_W, multiplexer_1_out, multiplexer_5_out, or_6_out, register_5_q, STORE_BYTE_W;
  wire [23:0] adder_1_out, adder_3_out, counter_1_q, INIT_ADDR_IN, IR_ADDR_IN, KEY_ADDR_IN, LOAD_ADDR_IN,
       multiplexer_3_out, multiplier_1_out, register_1_q, STORE_ADDR_IN;
  wire [31:0] bit_extender_1_out, INIT_BITS_IN, IR_DATA_OUT, KEY_BITS_IN, LOAD_DATA_OUT, main_1_bits_out,
       multiplexer_2_out, STORE_BITS_IN, TTY_DATA_OUT;

  Clock clock_1 (.out(CLK));
  D_Flip_Flop d_ff_1 (.clk(CLK), .D(KEYBOARD_PURGE), .Q(d_ff_1_q));  // open: Qn, preset, en, reset
  or or_1 (or_1_out, d_ff_1_q, and_3_out);
  D_Flip_Flop d_ff_2 (.clk(CLK), .D(d_ff_7_q), .Q(d_ff_2_q));  // open: Qn, preset, en, reset
  Counter #(.width(24), .max('hffffff)) counter_1 (
    .count(KEYBOARD_PURGE), .Q(counter_1_q), .clk(CLK));  // open: load, D, carry, clr
  D_Flip_Flop d_ff_3 (.clk(CLK), .D(or_2_out), .Q(POWERED), .en(1'b1));  // open: Qn, preset, reset
  or or_2 (or_2_out, POWERED, ACTIVATE);
  Adder #(.width(24)) adder_1 (.a(ROM_ADDR), .b(24'h1), .out(adder_1_out));  // open: cin, cout
  or or_3 (or_3_out, d_ff_2_q, INIT_TOKEN_OUT);
  D_Flip_Flop d_ff_4 (.clk(CLK), .D(d_ff_2_q), .Q(d_ff_4_q));  // open: Qn, preset, en, reset
  D_Flip_Flop d_ff_5 (.clk(CLK), .D(INIT_TOKEN_OUT), .Q(d_ff_5_q));  // open: Qn, preset, en, reset
  Adder #(.width(24)) adder_2 (.a(counter_1_q), .b(24'h100004), .out(KEY_ADDR_IN));  // open: cin, cout
  Register #(.width(24)) register_1 (.D(ROM_DATA[23:0]), .en(d_ff_7_q), .Q(register_1_q), .clk(CLK));  // open: clr
  Register #(.width(24)) register_2 (.D(adder_1_out), .en(or_3_out), .Q(ROM_ADDR), .clk(CLK));  // open: clr
  Register #(.width(32)) register_3 (.D(ROM_DATA), .en(and_2_out), .Q(INIT_BITS_IN), .clk(CLK));  // open: clr
  assign bit_extender_1_out = {{25{1'b0}}, KEYBOARD_READ};  // Bit_Extender bit_extender_1
  and and_1 (and_1_out, ~POWERED, ACTIVATE);  // AND_Gate
  Comparator #(.width(24), .mode("unsigned")) comparator_1 (
    .a(multiplier_1_out), .b(adder_3_out), .eq(RUNNING), .lt(comparator_1_lt));  // open: gt
  D_Flip_Flop d_ff_6 (.clk(CLK), .D(or_4_out), .Q(d_ff_6_q));  // open: Qn, preset, en, reset
  or or_4 (or_4_out, d_ff_4_q, d_ff_5_q);
  Shifter #(.width(32)) shifter_1 (.in(bit_extender_1_out), .\dist (5'b11000), .out(KEY_BITS_IN));
  D_Flip_Flop d_ff_7 (.clk(CLK), .D(and_1_out), .Q(d_ff_7_q), .en(1'b1));  // open: Qn, preset, reset
  Adder #(.width(24)) adder_3 (.a(register_1_q), .b(24'h4), .out(adder_3_out));  // open: cin, cout
  and and_2 (and_2_out, comparator_1_lt, d_ff_6_q);
  cpu_main or1k___CPU (
    .LOAD_TOKEN_IN(LOAD_TOKEN_OUT), .FTIN(INIT_CYCLE), .LOAD_DATA(LOAD_DATA_OUT), .TIN(or_1_out), .CLK(CLK),
    .STORE_TOKEN_IN(STORE_TOKEN_OUT), .RAMIRIN(IR_DATA_OUT), .TRAMIRIN(IR_TOKEN_OUT),
    .LOAD_BYTE_W(LOAD_BYTE_W), .LOAD_TOKEN_OUT(LOAD_SEL_IN[1]), .LOAD_ADDR(LOAD_ADDR_IN),
    .STORE_TOKEN_OUT(STORE_SEL_IN[1]), .STORE_DATA(STORE_BITS_IN), .STORE_BYTE_W(STORE_BYTE_W),
    .STORE_ADDR(STORE_ADDR_IN), .RAMIRADDR(IR_ADDR_IN), .TRAMIROUT(IR_SEL_IN[0]), .TOUT(or1k___CPU_tout));
  D_Flip_Flop d_ff_8 (.clk(CLK), .D(TTY_TOKEN_OUT), .Q(TTY_OUTPUT));  // open: Qn, preset, en, reset
  and and_3 (and_3_out, d_ff_10_q, ~KETBOARD_AVAL);  // AND_Gate
  and and_4 (INIT_CYCLE, RUNNING, d_ff_6_q);
  D_Flip_Flop d_ff_9 (.clk(CLK), .D(and_2_out), .Q(INIT_TOKEN_IN));  // open: Qn, preset, en, reset
  D_Flip_Flop d_ff_10 (.clk(CLK), .D(CLEAR_TOKEN_OUT), .Q(d_ff_10_q));  // open: Qn, preset, en, reset
  and and_5 (KEY_SEL_IN[2], KETBOARD_AVAL, d_ff_10_q);
  Multiplier #(.width(24)) multiplier_1 (.a(ROM_ADDR), .b(24'h4), .out(multiplier_1_out));  // open: cin, cout
  D_Flip_Flop d_ff_11 (.clk(CLK), .D(or1k___CPU_tout), .Q(TTY_SEL_IN[2]));  // open: Qn, preset, en, reset
  Subtractor #(.width(24)) subtractor_1 (.a(multiplier_1_out), .b(24'h4), .out(INIT_ADDR_IN));  // open: bin, bout
  Register #(.width(7)) register_4 (.D(TTY_DATA_OUT[6:0]), .en(TTY_TOKEN_OUT), .Q(TTY_ASCII), .clk(CLK));  // open: clr
  Multiplexer #(.select(4), .width(4), .disabled(0)) multiplexer_1 (
    .in0(4'b0100), .in1(4'b0100), .in2(LOAD_BYTE_W), .in3(STORE_BYTE_W), .in4(4'b0001), .in5(4'b0001),
    .in6(4'b0001), .out(multiplexer_1_out), .sel(multiplexer_5_out), .en(or_7_out));  // open: in7, in8, in9, in10, in11, in12, in13, in14, in15
  Multiplexer #(.select(4), .width(32), .disabled(0)) multiplexer_2 (
    .in0(INIT_BITS_IN), .in3(STORE_BITS_IN), .in5({32{1'b0}}), .in6(KEY_BITS_IN), .out(multiplexer_2_out),
    .sel(multiplexer_5_out), .en(or_7_out));  // open: in1, in2, in4, in7, in8, in9, in10, in11, in12, in13, in14, in15
  Multiplexer #(.select(4), .width(24), .disabled(0)) multiplexer_3 (
    .in0(INIT_ADDR_IN), .in1(IR_ADDR_IN), .in2(LOAD_ADDR_IN), .in3(STORE_ADDR_IN), .in4(24'h100000),
    .in5(24'h100000), .in6(KEY_ADDR_IN), .out(multiplexer_3_out), .sel(multiplexer_5_out), .en(or_7_out));  // open: in7, in8, in9, in10, in11, in12, in13, in14, in15
  Multiplexer #(.select(4), .disabled(0)) multiplexer_4 (
    .in0(1'b1), .in1(1'b0), .in2(1'b0), .in3(1'b1), .in4(1'b0), .in5(1'b1), .in6(1'b1),
    .out(multiplexer_4_out), .sel(multiplexer_5_out), .en(or_7_out));  // open: in7, in8, in9, in10, in11, in12, in13, in14, in15
  Demultiplexer #(.select(4), .disabled(0)) demultiplexer_1 (
    .out0(INIT_TOKEN_OUT), .out1(IR_TOKEN_OUT), .out2(LOAD_TOKEN_OUT), .out3(STORE_TOKEN_OUT),
    .out4(TTY_TOKEN_OUT), .out5(CLEAR_TOKEN_OUT), .out6(KEYBOARD_PURGE), .in(main_1_tout),
    .sel(multiplexer_5_out), .en(main_1_tout));  // open: out7, out8, out9, out10, out11, out12, out13, out14, out15
  Demultiplexer #(.select(4), .width(32), .disabled(0)) demultiplexer_2 (
    .out1(IR_DATA_OUT), .out2(LOAD_DATA_OUT), .out4(TTY_DATA_OUT), .in(main_1_bits_out),
    .sel(multiplexer_5_out), .en(main_1_tout));  // open: out0, out3, out5, out6, out7, out8, out9, out10, out11, out12, out13, out14, out15
  ram_main main_1 (
    .TIN(or_8_out), .TOUT(main_1_tout), .CLEAR(and_1_out), .ADDRESS(multiplexer_3_out), .CLK(CLK),
    .STORE(multiplexer_4_out), .BYTE_OPSIZE(multiplexer_1_out), .BITS_IN(multiplexer_2_out),
    .BITS_OUT(main_1_bits_out));
  or or_5 (or_5_out, main_1_tout, or_8_out);
  assign or_6_out = 4'b0000 | {3'b000, IR_SEL_IN[0]} | {2'b00, LOAD_SEL_IN[1], 1'b0} | {2'b00, {2{STORE_SEL_IN[1]}}} | {1'b0, TTY_SEL_IN[2], 2'b00} | {1'b0, TTY_OUTPUT, 1'b0, TTY_OUTPUT} | {1'b0, {2{KEY_SEL_IN[2]}}, 1'b0};  // OR_Gate or_6, 4 bits wide
  D_Flip_Flop d_ff_12 (.clk(or_5_out), .D(or_8_out), .Q(d_ff_12_q));  // open: Qn, preset, en, reset
  or or_7 (or_7_out, d_ff_12_q, or_8_out);
  Multiplexer #(.width(4), .disabled(0)) multiplexer_5 (
    .in0(register_5_q), .in1(or_6_out), .out(multiplexer_5_out), .sel(or_8_out), .en(1'b1));
  Register #(.width(4)) register_5 (.D(or_6_out), .en(or_8_out), .Q(register_5_q), .clk(CLK));  // open: clr
  or or_8 (or_8_out, INIT_TOKEN_IN, IR_SEL_IN[0], LOAD_SEL_IN[1], STORE_SEL_IN[1], TTY_SEL_IN[2], TTY_OUTPUT, KEY_SEL_IN[2]);

  // Other names for the same wires on the sheet: CLEAR_SEL_IN (some bits) = {2{TTY_OUTPUT}};
  //   CLEAR_TOKEN_IN = TTY_OUTPUT; IR_TOKEN_IN = IR_SEL_IN[0]; KEY_SEL_IN[1] = KEY_SEL_IN[2];
  //   KEY_TOKEN_IN = KEY_SEL_IN[2]; KEY_TOKEN_OUT = KEYBOARD_PURGE; LOAD_TOKEN_IN = LOAD_SEL_IN[1];
  //   STORE_SEL_IN[0] = STORE_SEL_IN[1]; STORE_TOKEN_IN = STORE_SEL_IN[1]; TTY_TOKEN_IN = TTY_SEL_IN[2]
endmodule
